# Fritzing sketch edge_wiring_diagram (saved by Fritzing 1.0.6)
breadboards: 1

parts:
  ESP-H2-Devkitm-1 = ESP32 H2-DevKitM-1
  Aktiv_Buzzer = Passive Buzzer
  Knapp = Pushbutton [package="[SMD]"]
  RGB_LED = RGB LED (com. cathode, rgb) [color="Red (633nm)" current=0.030A package="5 mm [THT]"]
  R1 = Resistor [tolerance=±5% power=0.25W resistance=330 package=THT]
  R2 = Resistor [tolerance=±5% power=0.25W resistance=220 package=THT]
  R3 = Resistor [tolerance=±5% power=0.25W resistance=220 package=THT]
  Pin_layout_on_BMA400_part_GND_3_3V_SDA_SCL_ADDR_Opposite_side_use_INT1_on_real_part = 3-Axis Accelerometer Breakout - MMA8452Q
  R4 = Resistor [tolerance=±5% power=0.25W resistance=100 package=THT]

nets:
  N1: ESP-H2-Devkitm-1.Pin_1, Pin_layout_on_BMA400_part_GND_3_3V_SDA_SCL_ADDR_Opposite_side_use_INT1_on_real_part.SDA
  N2: ESP-H2-Devkitm-1.Pin_3, R3.Pin_1
  N3: ESP-H2-Devkitm-1.Pin_4, R2.Pin_1
  N4: ESP-H2-Devkitm-1.Pin_5, R1.Pin_1
  N5: ESP-H2-Devkitm-1.Pin_9, Knapp.Pin_3, Knapp.Pin_4
  N6: ESP-H2-Devkitm-1.Pin_10, R4.Pin_1
  N7: ESP-H2-Devkitm-1.Pin_13, ESP-H2-Devkitm-1.Pin_15, ESP-H2-Devkitm-1.Pin_16, ESP-H2-Devkitm-1.Pin_19, ESP-H2-Devkitm-1.Pin_30, Knapp.Pin_1, Knapp.Pin_2, RGB_LED.blue_anode, Pin_layout_on_BMA400_part_GND_3_3V_SDA_SCL_ADDR_Opposite_side_use_INT1_on_real_part.3.3V, Pin_layout_on_BMA400_part_GND_3_3V_SDA_SCL_ADDR_Opposite_side_use_INT1_on_real_part.I1
  N8: ESP-H2-Devkitm-1.Pin_21, Aktiv_Buzzer.-
  N9: ESP-H2-Devkitm-1.Pin_23, Pin_layout_on_BMA400_part_GND_3_3V_SDA_SCL_ADDR_Opposite_side_use_INT1_on_real_part.I2
  N10: ESP-H2-Devkitm-1.Pin_25, Pin_layout_on_BMA400_part_GND_3_3V_SDA_SCL_ADDR_Opposite_side_use_INT1_on_real_part.SCL
  N11: Aktiv_Buzzer.S, R4.Pin_0
  N12: RGB_LED.red_anode, R1.Pin_0
  N13: RGB_LED.common_cathode, R2.Pin_0
  N14: RGB_LED.green_anode, R3.Pin_0

custom parts:
  ESP32 H2-DevKitM-1: ESP32-H2-DevKitM-1 is an entry-level development board based on Bluetooth® Low Energy and IEEE 802.15.4 combo module ESP32-H2-MINI-1 or ESP32-H2-MINI-1U.
